# Fritzing sketch Board 06 (saved by Fritzing 0.9.10b)
breadboards: 2

parts:
  R1 = Resistor [tolerance=±1% power=0.5W resistance=10k package=THT]
  C1 = Electrolytic Capacitor [capacitance=10µF voltage=25V package="100 mil [THT, electrolytic]"]  # not connected
  Part1 = Adafruit KB2040

nets:
  N1: R1.Pin_0, Part1.D4
  N2: R1.Pin_1, Part1.A1
