# Fritzing sketch Board 07 (saved by Fritzing 0.9.10b)
breadboards: 2

parts:
  C1 = Electrolytic Capacitor [capacitance=10µF voltage=25V package="100 mil [THT, electrolytic]"]  # not connected
  Part1 = Adafruit KB2040
  R1 = Resistor [tolerance=±1% power=0.5W resistance=10k package=THT]

nets:
  N1: Part1.A1, R1.Pin_1
  N2: Part1.D4, R1.Pin_0
