# Fritzing sketch Board 15 (saved by Fritzing 0.9.10b)
breadboards: 2

parts:
  C1 = Electrolytic Capacitor [capacitance=10µF voltage=25V package="100 mil [THT, electrolytic]"]  # not connected
  Part1 = Adafruit KB2040
  R2 = Resistor [tolerance=±1% power=0.5W resistance=10k package=THT]
  U2 = AD9833 Module [mpn=AD9833 mn=AITRIP]
  U3 = LM358 [package=dip08]

nets:
  N1: Part1.GND, U2.DGND, U2.AGND, U3.G$1_V+
  N2: Part1.D10, U2.FSYNC
  N3: Part1.MOSI, U2.SDATA
  N4: Part1.SCLK, U2.SCLK
  N5: Part1.A0, U3.G$2_+IN
  N6: Part1.A1, R2.Pin_1
  3.3V: Part1.3.3V, U2.VCC, U3.G$1_V-
  N7: Part1.D4, R2.Pin_0
  N8: U2.OUT, U3.G$2_OUT

custom parts:
  AD9833 Module: programmable waveform generator
