# Fritzing sketch Board 21 (saved by Fritzing 0.9.10b)
breadboards: 2

parts:
  C1 = Electrolytic Capacitor [capacitance=10µF voltage=25V package="100 mil [THT, electrolytic]"]  # not connected
  Part1 = Adafruit KB2040
  R2 = Resistor [tolerance=±1% power=0.5W resistance=10k package=THT]
  U2 = AD9833 Module [mpn=AD9833 mn=AITRIP]
  U3 = LM358 [package=dip08]
  R3 = Resistor [tolerance=±1% power=0.5W resistance=10k package=THT]
  R4 = Resistor [tolerance=±1% power=0.5W resistance=10k package=THT]
  R5 = Resistor [tolerance=±1% power=0.5W resistance=10k package=THT]
  R6 = Resistor [tolerance=±1% power=0.5W resistance=10k package=THT]
  R7 = Resistor [tolerance=±1% power=0.5W resistance=330 package=THT]
  Part2 = Adafruit INA219 [part_number="Adafruit #904"]

nets:
  GND: Part1.GND, U2.DGND, U2.AGND, U3.G$1_V+, R6.Pin_1, Part2.GND
  N1: Part1.D10, U2.FSYNC
  N2: Part1.MOSI, U2.SDATA
  N3: Part1.SCLK, U2.SCLK
  N4: Part1.A0, U3.G$2_+IN, R3.Pin_0, R7.Pin_0
  N5: Part1.A1, R2.Pin_1
  N6: Part1.A2, Part2.SDA
  N7: Part1.A3, Part2.SCL
  VCC: Part1.3.3V, U2.VCC, U3.G$1_V-, Part2.VIN+, Part2.VCC
  N8: Part1.D4, R2.Pin_0
  N9: U2.OUT, U3.G$2_OUT
  N10: U3.G$2_-IN, R5.Pin_1, R6.Pin_0
  N11: R3.Pin_1, R4.Pin_1
  N12: R4.Pin_0, R5.Pin_0

custom parts:
  AD9833 Module: programmable waveform generator
  Adafruit INA219: This breakout board will solve all your power-monitoring problems. Instead of struggling with two multimeters, you can just use the handy INA219B chip on this breakout to both measure both the high side voltage and DC current draw over I2C with 1% precision. Most current-measuring devices such as our current panel meter are only good for low side measuring. That means that unless you want to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
