# Fritzing sketch Board 39a (saved by Fritzing 0.9.10b)
breadboards: 2

parts:
  C1 = Electrolytic Capacitor [capacitance=10µF voltage=25V package="100 mil [THT, electrolytic]"]  # not connected
  Part1 = Adafruit KB2040
  R2 = Resistor [tolerance=±1% power=0.5W resistance=10k package=THT]
  U2 = AD9833 Module [mpn=AD9833 mn=AITRIP]
  U3 = LM358 [package=dip08]
  R3 = Resistor [tolerance=±1% power=0.5W resistance=10k package=THT]
  R4 = Resistor [tolerance=±1% power=0.5W resistance=10k package=THT]
  R5 = Resistor [tolerance=±1% power=0.5W resistance=10k package=THT]
  R6 = Resistor [tolerance=±1% power=0.5W resistance=10k package=THT]
  R7 = Resistor [tolerance=±1% power=0.5W resistance=330 package=THT]
  Part2 = Adafruit INA219 [part_number="Adafruit #904"]
  Part3 = Adafruit MCP4725 [part_number="Adafruit #935"]
  Adafruit#1 = Adafruit ADS1115 16-Bit ADC [part_number=1085]
  Q1 = TRANSISTOR_NPN [package=to-92-ammo]
  R8 = Resistor [tolerance=±5% power=0.25 resistance=47 package=THT]
  R9 = Resistor [tolerance=±5% power=0.25 resistance=56 package=THT]
  R10 = Resistor [tolerance=±5% power=0.25 resistance=68k package=THT]
  R11 = Resistor [tolerance=±1% power=0.5W resistance=330 package=THT]
  D1 = Diode [package=diode-1n4001]
  R12 = Resistor [tolerance=±1% power=0.5W resistance=10 package=THT]  # not connected
  Q2 = TRANSISTOR_NPN [package=to-92-ammo]
  R13 = Resistor [tolerance=±1% power=0.5W resistance=1k package=THT]
  R14 = Resistor [tolerance=±1% power=0.5W resistance=1k package=THT]
  R15 = Resistor [tolerance=±1% power=0.5W resistance=100 package=THT]
  R16 = Resistor [tolerance=±1% power=0.5W resistance=10 package=THT]
  C2 = Capacitor [mn="ceramic 100 nf" package=cap-pth-small2]
  L1 = Inductor [package="0805 [SMD]"]

nets:
  GND: Part1.GND, U2.DGND, U2.AGND, U3.G$1_V+, R6.Pin_1, Part2.GND, Part3.GND, Adafruit#1.GND, Q1.E, D1.C, Q2.E, R15.Pin_1
  VCC: Part1.3.3V, U2.VCC, U3.G$1_V-, Part2.VCC, Part2.VIN+, Part3.VCC, Adafruit#1.VCC, R13.Pin_0
  N1: Part1.D10, U2.FSYNC
  N2: Part1.MOSI, U2.SDATA
  N3: Part1.SCLK, U2.SCLK
  N4: Part1.A0, R15.Pin_0, R16.Pin_0
  N5: Part1.A1, R2.Pin_1
  N6: Part1.A2, Part2.SDA, Part3.SDA, Adafruit#1.SDA
  N7: Part1.A3, Part2.SCL, Part3.SCL, Adafruit#1.SCL
  N8: Part1.D4, R2.Pin_0
  N9: U2.OUT, U3.G$2_OUT
  N10: U3.G$2_+IN, R3.Pin_0, R7.Pin_0, L1.pin_0
  N11: U3.G$2_-IN, R5.Pin_1, R6.Pin_0
  N12: R3.Pin_1, R4.Pin_1
  N13: R4.Pin_0, R5.Pin_0
  N14: Q1.B, R11.Pin_1
  N15: Q1.C, R8.Pin_0, R9.Pin_0, R10.Pin_0
  N16: Q2.B, R14.Pin_1
  N17: Q2.C, R13.Pin_1
  N18: R16.Pin_1, C2.2
  N19: C2.1, L1.pin_1

custom parts:
  AD9833 Module: programmable waveform generator
  Adafruit INA219: This breakout board will solve all your power-monitoring problems. Instead of struggling with two multimeters, you can just use the handy INA219B chip on this breakout to both measure both the high side voltage and DC current draw over I2C with 1% precision. Most current-measuring devices such as our current panel meter are only good for low side measuring. That means that unless you want to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
  Adafruit MCP4725: Your microcontroller probably has an ADC (analog -> digital converter) but does it have a DAC (digital -> analog converter)??? Now it can! This breakout board features the easy-to-use MCP4725 12-bit DAC. Control it via I2C and send it the value you want it to output, and the VOUT pin will have it. Great for audio / analog projects, such as when you can't use PWM but need a sine wave or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
  Adafruit ADS1115 16-Bit ADC: For microcontrollers without an analog-to-digital converter or when you want a higher-precision ADC, the ADS1115 provides 16-bit precision at 860 samples/second over I2C. The chip can be configured as 4 single-ended input channels, or two differential channels. As a nice bonus, it even includes a programmable gain amplifier, up to x16, to help boost up smaller single/differential signals to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
