# Fritzing sketch Board 44 (saved by Fritzing 0.9.10b)
breadboards: 1

parts:
  R1 = Resistor [tolerance=±1% power=0.5W resistance=1k package=THT]
  Part1 = Adafruit KB2040

nets:
  N1: R1.Pin_1, Part1.A0
  N2: Part1.SDA, Part1.SCL
