# Fritzing sketch Board 45 (saved by Fritzing 0.9.10b)
breadboards: 1

parts:
  R1 = Resistor [tolerance=±1% power=0.5W resistance=1k package=THT]
  Part1 = Adafruit KB2040
  Part2 = Adafruit DRV8833 DC/Stepper Motor Driver [part_number="Adafruit #3297"]

nets:
  N1: R1.Pin_0, Part2.BOUT1
  N2: R1.Pin_1, Part1.A0
  GND: Part1.GND, Part2.GND
  N3: Part1.SDA, Part1.SCL
  N4: Part1.RAW, Part2.VMOTOR
  N5: Part1.D6, Part2.!SLEEP
  N6: Part1.D8, Part2.BIN1
  N7: Part1.D9, Part2.BIN2

custom parts:
  Adafruit DRV8833 DC/Stepper Motor Driver: Spin two DC motors or step one bi-polar or uni-polar stepper with up to 1.2A per channel using the DRV8833. This motor driver chip is a nice alternative to the TB6612 driver. Like that chip, you get 2 full H-bridges, but this chip is better for low voltage uses (can run from 2.7V up to 10.8V motor power) and has built in current limiting capability. We set it up for 1A current limiting so you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
